// Logisim project Memory-Project.circ as structural Verilog: 11 circuits, main circuit main
module main (
);

  wire clock_1_out, d_ff_1_p2;

  Clock clock_1 (.out(clock_1_out));
  // D_Flip_Flop #(.trigger("falling")) d_ff_1: pin names not known; wires that end beside it: clock_1_out, d_ff_1_p2
  D_Flip_Flop #(.trigger("falling")) d_ff_2 ();  // open: clk, D, Q, Qn, preset, en, reset
  D_Flip_Flop #(.trigger("falling")) d_ff_3 ();  // open: clk, D, Q, Qn, preset, en, reset
  D_Flip_Flop #(.trigger("falling")) d_ff_4 ();  // open: clk, D, Q, Qn, preset, en, reset
  D_Flip_Flop #(.trigger("falling")) d_ff_5 ();  // open: clk, D, Q, Qn, preset, en, reset
  D_Flip_Flop #(.trigger("falling")) d_ff_6 ();  // open: clk, D, Q, Qn, preset, en, reset
  D_Flip_Flop #(.trigger("falling")) d_ff_7 ();  // open: clk, D, Q, Qn, preset, en, reset
  D_Flip_Flop #(.trigger("falling")) d_ff_8 ();  // open: clk, D, Q, Qn, preset, en, reset
  D_Flip_Flop #(.trigger("falling")) d_ff_9 ();  // open: clk, D, Q, Qn, preset, en, reset
  D_Flip_Flop #(.trigger("falling")) d_ff_10 ();  // open: clk, D, Q, Qn, preset, en, reset
  D_Flip_Flop #(.trigger("falling")) d_ff_11 ();  // open: clk, D, Q, Qn, preset, en, reset
  D_Flip_Flop #(.trigger("falling")) d_ff_12 ();  // open: clk, D, Q, Qn, preset, en, reset
endmodule

module counter (
  input  in_1,
  input  [11:0] D_input,
  output [11:0] \output 
);

  wire clock_out, comparator_1_gt, or_1_out;
  wire [11:0] complementary_2_12_bit_lookahead_adder_1_out_4;

  Comparator #(.width(12)) comparator_1 (.a(\output ), .b(D_input), .gt(comparator_1_gt));  // open: eq, lt
  Clock clock (.out(clock_out));
  complementary_2_12_bit_lookahead_adder complementary_2_12_bit_lookahead_adder_1 (
    .in_1(\output ), .rt({12{1'b0}}), .in_2(1'b1), .out_4(complementary_2_12_bit_lookahead_adder_1_out_4));  // open: out_6, overflow
  or or_1 (or_1_out, \output [1], comparator_1_gt);
  _12_bit_Register u_12_bit_register_1 (.Reset(or_1_out), .C(clock_out), .Q(\output ));
  // Pins of 2 and 12 bits meet at \output 
endmodule

module _12_bit_Register (
  input  Reset,
  input  Write,
  input  C,
  output [11:0] Q
);

  wire d_ff_2_qn, d_ff_4_qn, d_ff_7_qn, d_ff_12_qn, d_ff_14_qn, undriven_2, undriven_3, undriven_4,
       undriven_5, undriven_6, undriven_7;
  wire [11:0] undriven;

  D_Flip_Flop #(.trigger("falling")) d_ff_1 (
    .clk(C), .D(undriven[0]), .Q(Q[0]), .en(undriven_7), .reset(Reset));  // open: Qn, preset
  D_Flip_Flop #(.trigger("falling")) d_ff_2 (
    .clk(C), .D(undriven[1]), .Q(Q[1]), .Qn(d_ff_2_qn), .preset(undriven_2), .en(undriven_7), .reset(Reset));
  D_Flip_Flop #(.trigger("falling")) d_ff_3 (
    .clk(C), .D(undriven[1]), .Q(Q[1]), .Qn(d_ff_2_qn), .preset(undriven_2), .en(undriven_7), .reset(Reset));
  D_Flip_Flop #(.trigger("falling")) d_ff_4 (
    .clk(C), .D(undriven[2]), .Q(Q[2]), .Qn(d_ff_4_qn), .preset(undriven_3), .en(undriven_7), .reset(Reset));
  D_Flip_Flop #(.trigger("falling")) d_ff_5 (
    .clk(C), .D(undriven[2]), .Q(Q[2]), .Qn(d_ff_4_qn), .preset(undriven_3), .en(undriven_7), .reset(Reset));
  D_Flip_Flop #(.trigger("falling")) d_ff_6 (
    .clk(C), .D(undriven[3]), .Q(Q[3]), .en(undriven_7), .reset(Reset));  // open: Qn, preset
  D_Flip_Flop #(.trigger("falling")) d_ff_7 (
    .clk(C), .D(undriven[5]), .Q(Q[5]), .Qn(d_ff_7_qn), .preset(undriven_4), .en(undriven_7), .reset(Reset));
  D_Flip_Flop #(.trigger("falling")) d_ff_8 (
    .clk(C), .D(undriven[5]), .Q(Q[5]), .Qn(d_ff_7_qn), .preset(undriven_4), .en(undriven_7), .reset(Reset));
  D_Flip_Flop #(.trigger("falling")) d_ff_9 (
    .clk(C), .D(undriven[6]), .Q(Q[6]), .en(undriven_7), .reset(Reset));  // open: Qn, preset
  D_Flip_Flop #(.trigger("falling")) d_ff_10 (
    .clk(C), .D(undriven[7]), .Q(Q[7]), .en(undriven_7), .reset(Reset));  // open: Qn, preset
  D_Flip_Flop #(.trigger("falling")) d_ff_11 (
    .clk(C), .D(undriven[8]), .Q(Q[8]), .en(undriven_7), .reset(Reset));  // open: Qn, preset
  D_Flip_Flop #(.trigger("falling")) d_ff_12 (
    .clk(C), .D(undriven[9]), .Q(Q[9]), .Qn(d_ff_12_qn), .preset(undriven_5), .en(undriven_7), .reset(Reset));
  D_Flip_Flop #(.trigger("falling")) d_ff_13 (
    .clk(C), .D(undriven[9]), .Q(Q[9]), .Qn(d_ff_12_qn), .preset(undriven_5), .en(undriven_7), .reset(Reset));
  D_Flip_Flop #(.trigger("falling")) d_ff_14 (
    .clk(C), .D(undriven[10]), .Q(Q[10]), .Qn(d_ff_14_qn), .preset(undriven_6), .en(undriven_7), .reset(Reset));
  D_Flip_Flop #(.trigger("falling")) d_ff_15 (
    .clk(C), .D(undriven[10]), .Q(Q[10]), .Qn(d_ff_14_qn), .preset(undriven_6), .en(undriven_7), .reset(Reset));
  D_Flip_Flop #(.trigger("falling")) d_ff_16 (
    .clk(C), .D(undriven[11]), .Q(Q[11]), .en(undriven_7), .reset(Reset));  // open: Qn, preset
endmodule

module Register_File (
);

  _12_bit_Register u_12_bit_register_1 ();  // open: Reset, C, Q
  _12_bit_Register u_12_bit_register_2 ();  // open: Reset, C, Q
  _12_bit_Register u_12_bit_register_3 ();  // open: Reset, C, Q
  _12_bit_Register u_12_bit_register_4 ();  // open: Reset, C, Q
  _12_bit_Register u_12_bit_register_5 ();  // open: Reset, C, Q
  _12_bit_Register u_12_bit_register_6 ();  // open: Reset, C, Q
  _12_bit_Register u_12_bit_register_7 ();  // open: Reset, C, Q
  _12_bit_Register u_12_bit_register_8 ();  // open: Reset, C, Q
endmodule

module complementary_2_12_bit_lookahead_adder (
  input  [11:0] in_1,
  input  in_2,
  input  [11:0] rt,
  output [11:0] out_4,
  output overflow,
  output out_6
);

  wire n4_bit_lookahead_adder_1_out_5, n4_bit_lookahead_adder_2_out_5;
  wire [3:0] n4_bit_lookahead_adder_1_out_3, n4_bit_lookahead_adder_2_out_3, n4_bit_lookahead_adder_3_out_3;
  wire [11:0] n4_bit_lookahead_adder_3_r;

  // _12_bit_Register r3: pin names not known
  _12_bit_Register r5 ();  // open: Reset, C, Q
  _4_bit_lookahead_adder u_4_bit_lookahead_adder_1 (
    .in_2({rt[3], in_1[3], rt[2], in_1[2], rt[1], in_1[1], rt[0], in_1[0]}), .in_1(in_2),
    .out_5(n4_bit_lookahead_adder_1_out_5), .out_3(n4_bit_lookahead_adder_1_out_3));  // open: R
  _4_bit_lookahead_adder u_4_bit_lookahead_adder_2 (
    .in_2({rt[7], in_1[7], rt[6], in_1[6], rt[5], in_1[5], rt[4], in_1[4]}),
    .in_1(n4_bit_lookahead_adder_1_out_5), .out_5(n4_bit_lookahead_adder_2_out_5),
    .out_3(n4_bit_lookahead_adder_2_out_3));  // open: R
  _4_bit_lookahead_adder u_4_bit_lookahead_adder_3 (
    .in_2({rt[11], in_1[11], rt[10], in_1[10], rt[9], in_1[9], rt[8], in_1[8]}),
    .in_1(n4_bit_lookahead_adder_2_out_5), .out_5(out_6), .out_3(n4_bit_lookahead_adder_3_out_3),
    .R(n4_bit_lookahead_adder_3_r));
  xor xor_1 (overflow, n4_bit_lookahead_adder_3_r[0], out_6);
  // Pins of 1 and 12 bits meet at n4_bit_lookahead_adder_3_r
endmodule

module C1 (
  input  in_1,
  input  [7:0] in_2,
  output out_3
);

  wire and_1_out, g0_out, p0_out;

  and g0 (g0_out, in_2[1], in_2[0]);
  or p0 (p0_out, in_2[1], in_2[0]);
  and and_1 (and_1_out, in_1, p0_out);
  or or_1 (out_3, g0_out, and_1_out);
endmodule

module C2 (
  input  in_1,
  input  [7:0] in_2,
  output out_3
);

  wire and_1_out, and_2_out, g0_out, g1_out, p0_out, p1_out;

  or p0 (p0_out, in_2[0], in_2[1]);
  and g0 (g0_out, in_2[0], in_2[1]);
  or p1 (p1_out, in_2[2], in_2[3]);
  and g1 (g1_out, in_2[3], in_2[2]);
  and and_1 (and_1_out, in_1, p0_out, p1_out);
  and and_2 (and_2_out, g0_out, p1_out);
  or or_1 (out_3, and_1_out, and_2_out, g1_out);
endmodule

module C3 (
  input  in_1,
  input  [7:0] in_2,
  output out_3
);

  wire and_1_out, and_2_out, and_3_out, g0_out, g1_out, g2_out, p0_out, p1_out, p2_out;

  or p0 (p0_out, in_2[1], in_2[0]);
  and g0 (g0_out, in_2[1], in_2[0]);
  or p1 (p1_out, in_2[3], in_2[2]);
  and g1 (g1_out, in_2[3], in_2[2]);
  or p2 (p2_out, in_2[5], in_2[4]);
  and g2 (g2_out, in_2[5], in_2[4]);
  and and_1 (and_1_out, in_1, p0_out, p1_out, p2_out);
  and and_2 (and_2_out, g0_out, p1_out, p2_out);
  and and_3 (and_3_out, g1_out, p2_out);
  or or_1 (out_3, and_1_out, and_2_out, and_3_out, g2_out);
endmodule

module C4 (
  input  C0,
  input  [7:0] in_2,
  output C4
);

  wire and_1_out, and_2_out, and_3_out, and_4_out, g0_out, g1_out, g2_out, g3_out, p0_out, p1_out, p2_out,
       p3_out;

  or p0 (p0_out, in_2[0], in_2[1]);
  and g0 (g0_out, in_2[0], in_2[1]);
  or p1 (p1_out, in_2[2], in_2[3]);
  and g1 (g1_out, in_2[2], in_2[3]);
  or p2 (p2_out, in_2[4], in_2[5]);
  and g2 (g2_out, in_2[4], in_2[5]);
  or p3 (p3_out, in_2[6], in_2[7]);
  and g3 (g3_out, in_2[7], in_2[6]);
  and and_1 (and_1_out, C0, p0_out, p1_out, p2_out, p3_out);
  and and_2 (and_2_out, g0_out, p1_out, p2_out, p3_out);
  and and_3 (and_3_out, g1_out, p2_out, p3_out);
  and and_4 (and_4_out, g2_out, p3_out);
  or or_1 (C4, and_1_out, and_2_out, and_3_out, and_4_out, g3_out);
endmodule

module _4_bit_lookahead_adder (
  input  in_1,
  input  [7:0] in_2,
  output [3:0] out_3,
  output [11:0] R,
  output out_5
);

  wire c1_1_out_3, c2_1_out_3;

  C1 c1_1 (.in_2(in_2), .in_1(in_1), .out_3(c1_1_out_3));
  C2 c2_1 (.in_2(in_2), .in_1(in_1), .out_3(c2_1_out_3));
  C3 c3_1 (.in_2(in_2), .in_1(in_1), .out_3(R[0]));
  C4 c4_1 (.in_2(in_2), .C0(in_1), .C4(out_5));
  _1_bit_adder u_1_bit_adder_1 (.A(in_2[0]), .Write(in_2[1]), .CARRY_IN(in_1), .SUM(out_3[0]));  // open: CARRY_OUT
  _1_bit_adder u_1_bit_adder_2 (
    .A(in_2[2]), .Write(in_2[3]), .CARRY_IN(c1_1_out_3), .SUM(out_3[1]));  // open: CARRY_OUT
  _1_bit_adder u_1_bit_adder_3 (
    .A(in_2[4]), .Write(in_2[5]), .CARRY_IN(c2_1_out_3), .SUM(out_3[2]));  // open: CARRY_OUT
  _1_bit_adder u_1_bit_adder_4 (.A(in_2[6]), .Write(in_2[7]), .CARRY_IN(R[0]), .SUM(out_3[3]));  // open: CARRY_OUT
  // Pins of 1 and 12 bits meet at R
endmodule

module _1_bit_adder (
  input  CARRY_IN,
  input  A,
  input  Write,
  output SUM,
  output CARRY_OUT
);

  wire and_1_out, and_2_out, and_3_out;

  xor xor_1 (SUM, CARRY_IN, A, Write);
  and and_1 (and_1_out, CARRY_IN, A);
  and and_2 (and_2_out, CARRY_IN, Write);
  and and_3 (and_3_out, A, Write);
  or or_1 (CARRY_OUT, and_1_out, and_2_out, and_3_out);

  // Notes on the sheet:
  //   B
endmodule
